# Fritzing sketch bluetooth_rgb_led (saved by Fritzing 0.9.3b)
breadboards: 1

parts:
  Part1 = Arduino Uno (Rev3) - ICSP
  Part2 = Bluetooth HC-05 Macho
  LED1 = RGB LED - (4 legs) [package="5 mm [THT]"]

nets:
  N1: Part1.D9_PWM, LED1.blue_cathode
  N2: Part1.D10_PWM/SS, LED1.green_cathode
  N3: Part1.D11_PWM/MOSI, LED1.red_cathode
  N4: Part1.D6_PWM, Part2.TXD
  N5: Part1.D7, Part2.RXD
  5V: Part1.5V, Part2.VCC
  GND: Part1.GND, Part2.GND, LED1.common_anode
